// Logisim project DataMemory.circ as structural Verilog: 1 circuit, main circuit main
module main (
  input  [31:0] address,
  input  [4:0] byte_writes,
  input  clk,
  input  [31:0] data_in,
  output [31:0] data_out
);

  wire [23:0] bitselector_1_out;

  BitSelector #(.group(24), .width(32)) bitselector_1 (.in(address), .out(bitselector_1_out), .sel(1'b0));
  // RAM #(.addrWidth(24), .line("quad")) ram_1: pin names not known; wires that end beside it: bitselector_1_out, clk
endmodule
