// Logisim project InstructionMemory.circ as structural Verilog: 1 circuit, main circuit main
module main (
  input  [31:0] address,
  output [31:0] data_out
);

  wire [9:0] bitselector_1_out;

  BitSelector #(.group(10), .width(32)) bitselector_1 (.in(address), .out(bitselector_1_out), .sel(2'b00));
  ROM #(.addrWidth(10), .dataWidth(32)) rom_1 (.addr(bitselector_1_out), .data(data_out));

  // Notes on the sheet:
  //   contents of rom_1 (hex, n*v repeats v):
  //   18193 ff117 dfc10113 40006f f00513 8067
endmodule
