// Logisim project RV32I.circ as structural Verilog: 1 circuit, main circuit main
module main (
  input  reset
);

  wire clk, comparator_1_eq, comparator_2_eq, decoder_1_out0, decoder_1_out1, decoder_1_out3, decoder_1_out4,
       decoder_1_out5, or_1_out, or_2_out;
  wire [0:0] decoder_1_out2;
  wire [2:0] f3, \type ;
  wire [3:0] main_4_out_2;
  wire [4:0] instructiondecoder_1_rd, instructiondecoder_1_rs1, instructiondecoder_1_rs2;
  wire [6:0] f7, instructiondecoder_1_opcode;
  wire [31:0] adder_1_out, B_Imm, I_Imm, J_Imm, main_1_data_out, main_2_rs1, main_2_rs2, main_3_d,
       main_5_data_out, main_6_out_3, multiplexer_1_out, multiplexer_2_out, multiplexer_3_out, PC_q, S_Imm,
       U_Imm;

  Adder #(.width(32)) adder_1 (.a(PC_q), .b(32'h1), .out(adder_1_out));  // open: cin, cout
  Multiplexer #(.enable("false"), .width(32)) multiplexer_1 (
    .in0(adder_1_out), .out(multiplexer_1_out), .sel(1'b0));  // open: in1
  Register #(.width(32)) PC (.D(multiplexer_1_out), .Q(PC_q), .clk(clk), .clr(reset));  // open: en
  // Probe on PC_q
  InstructionMemory_main main_1 (.data_out(main_1_data_out));  // open: address
  // Probe on main_1_data_out
  // Probe on \type 
  InstructionDecoder instructiondecoder_1 (
    .rd(instructiondecoder_1_rd), .funct3(f3), .rs1(instructiondecoder_1_rs1),
    .rs2(instructiondecoder_1_rs2), .funct7(f7), .opcode(instructiondecoder_1_opcode), .\type (\type ),
    .IImm(I_Imm), .SImm(S_Imm), .BImm(B_Imm), .UImm(U_Imm), .JImm(J_Imm), .Instruction(main_1_data_out));
  // Probe on instructiondecoder_1_rd
  // Probe on f3
  // Probe on instructiondecoder_1_rs1
  // Probe on instructiondecoder_1_rs2
  // Probe on f7
  // Probe on instructiondecoder_1_opcode
  // Probe on I_Imm
  // Probe on S_Imm
  // Probe on B_Imm
  // Probe on U_Imm
  // Probe on J_Imm
  Decoder #(.select(3)) decoder_1 (
    .out0(decoder_1_out0), .out1(decoder_1_out1), .out2(decoder_1_out2[0]), .out3(decoder_1_out3),
    .out4(decoder_1_out4), .out5(decoder_1_out5), .sel(\type ));  // open: out6, out7, en
  or or_1 (or_1_out, decoder_1_out0, decoder_1_out1);
  // Probe on instructiondecoder_1_opcode
  Clock Clock (.out(clk));
  RegFile_main main_2 (
    .rs1(main_2_rs1), .rs2(main_2_rs2), .sel_rs1(instructiondecoder_1_rs1),
    .sel_rs2(instructiondecoder_1_rs2), .write(or_1_out), .rd(instructiondecoder_1_rd), .rst(reset),
    .data(multiplexer_3_out), .clk(clk));
  Comparator #(.width(7)) comparator_1 (
    .a(instructiondecoder_1_opcode), .b(7'b0010001), .eq(comparator_1_eq));  // open: gt, lt
  Comparator #(.width(7)) comparator_2 (
    .a(instructiondecoder_1_opcode), .b(7'b0100011), .eq(comparator_2_eq));  // open: gt, lt
  // Probe on main_2_rs1
  // Probe on multiplexer_2_out
  Multiplexer #(.enable("false"), .select(3), .width(32)) multiplexer_2 (
    .in0(main_2_rs2), .in1(I_Imm), .in2(S_Imm), .in3(B_Imm), .in4(U_Imm), .in5(J_Imm),
    .out(multiplexer_2_out), .sel(\type ));  // open: in6, in7
  or or_2 (or_2_out, comparator_2_eq, comparator_1_eq);
  ALU_main main_3 (
    .d(main_3_d), .s1(main_2_rs1), .s2(multiplexer_2_out), .funct7(f7), .AddOveride(or_2_out), .funct3(f3));
  // Probe on multiplexer_3_out
  // Probe on main_3_d
  // Probe on {main_4_out_2, decoder_1_out2[0]}
  STypeSelector_main main_4 (.out_2(main_4_out_2));  // open: in_1
  // Probe on main_5_data_out
  DataMemory_main main_5 (
    .data_out(main_5_data_out), .address(main_3_d), .byte_writes({main_4_out_2, decoder_1_out2[0]}),
    .clk(clk), .data_in(main_2_rs2));
  LoadSelector_main main_6 (.out_3(main_6_out_3));  // open: in_1, in_2
  // Probe on main_6_out_3
  Multiplexer #(.enable("false"), .width(32)) multiplexer_3 (
    .in0(main_3_d), .in1(main_6_out_3), .out(multiplexer_3_out), .sel(comparator_1_eq));

  // Other names for the same wires on the sheet: rst = reset

  // Notes on the sheet:
  //   Add 1 because IMem 
  //   is accessible only in 
  //   multiples of 4 bytes 
  //   (since all instructions 
  //   are 32bits exactly)
endmodule
